# Fritzing sketch Fritzing (saved by Fritzing 0.9.3b)
breadboards: 1

parts:
  Part1 = Adafruit Metro M0 Express
  J1 = Basic Servo
  J2 = Basic Servo
  J3 = Basic Servo
  J4 = Basic Servo
  U1 = POT [package=3362u]
  U2 = POT [package=3362u]
  U3 = POT [package=3362u]
  U4 = POT [package=3362u]
  U5 = SWITCH_SPDT [package=kps-1290]
  USBTTL1 = USB TTL Serial Cable

nets:
  N1: Part1.A1, U4.S
  N2: Part1.A2, U3.S
  N3: Part1.A3, U2.S
  N4: Part1.A4, U1.S
  GND: Part1.GND, J1.gnd, J2.gnd, J3.gnd, J4.gnd, U1.E, U2.E, U3.E, U4.E, U5.O, USBTTL1.GND
  N5: Part1.D12, U5.P
  N6: Part1.D6, J2.pulse
  N7: Part1.D5, J1.pulse
  N8: Part1.D4, J3.pulse
  N9: Part1.D3, J4.pulse
  N10: Part1.D1, USBTTL1.RX
  N11: Part1.D0, USBTTL1.TX
  3.3V: Part1.3.3V, U1.A, U2.A, U3.A, U4.A, USBTTL1.5V
  VCC: Part1.+5V, J1.vcc, J2.vcc, J3.vcc, J4.vcc

custom parts:
  Adafruit Metro M0 Express: Metro is our series of microcontroller boards for use with the Arduino IDE. This new Metro board looks a whole lot like our original Metro 328, but with a huge upgrade. Instead of the ATmega328, this Metro features a ATSAMD21G18 chip, an ARM Cortex M0+. It's our first Metro that is designed for use with CircuitPython! CircuitPython is our beginner-oriented flavor of MicroPython - and as the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
